# Fritzing sketch fan-speed-controller (saved by Fritzing 0.9.3b)
circuit board: 5.18567cm x 5.43857cm
breadboards: 1

parts:
  ATTINY45 = ATTINY45 [package=dip]
  7805 = Voltage Regulator [package=to220-igo]
  PC847 = mystery part, 16 pins [chip_label=? part_number=PC847]
  1kΩ = Resistor [tolerance=±5% resistance=1k package=THT]
  Terminal_Block = Camdenboss CTB0158-7 [part_number=CTB0158-7 package=THT]
  1kΩ_2 = Resistor [tolerance=±5% resistance=1k package=THT]
  100nf = Ceramic Capacitor [capacitance=100nF package="100 mil [THT, multilayer]"]
  330nf = Ceramic Capacitor [capacitance=0pF package="100 mil [THT, multilayer]"]
  C = Pad [width=5 height=5 connect=south]
  C_2 = Pad [width=5 height=5 connect=center]
  10kΩ = Resistor [tolerance=±5% resistance=10k package=THT]
  220Ω = Resistor [tolerance=±5% resistance=220 package=THT]
  47nf = Ceramic Capacitor [capacitance=100n package="100 mil [THT, multilayer]"]

nets:
  N1: ATTINY45.PB5(NRES), 1kΩ.Pin_0
  N2: ATTINY45.PB3(ADC3), PC847.pin13
  N3: ATTINY45.PB4(ADC2), PC847.pin15
  GND: ATTINY45.GND, 7805.GND, 100nf.0, 330nf.0, 10kΩ.Pin_0
  N4: ATTINY45.PB0(MOSI), 1kΩ_2.Pin_0
  N5: ATTINY45.PB1(MISO), PC847.pin11
  N6: ATTINY45.PB2(SCK_ADC1), PC847.pin9
  N7: ATTINY45.VCC, 7805.OUT, PC847.pin10, PC847.pin12, PC847.pin14, PC847.pin16, 1kΩ.Pin_1, 100nf.1
  N8: 7805.IN, Terminal_Block.pin1, 330nf.1, C.pad, C_2.pad
  N9: PC847.pin1, Terminal_Block.pin5
  N10: PC847.pin2, PC847.pin4, PC847.pin6, PC847.pin8, Terminal_Block.pin6, 47nf.0
  N11: PC847.pin3, Terminal_Block.pin4
  N12: PC847.pin5, Terminal_Block.pin3
  N13: PC847.pin7, Terminal_Block.pin2
  N14: Terminal_Block.pin7, 220Ω.Pin_1, 47nf.1
  N15: 1kΩ_2.Pin_1, 10kΩ.Pin_1

notes:
  12V
  GND
  OUT
  SW1
  SW2
  SW3
  SW4
  Fan Motor
  Speed Controller
  ©2022 That Ain't Working
  B
  E
